# Fritzing sketch car_connected (saved by Fritzing 0.9.3b)

parts:
  Mod1 = Arduino Sensor Shield v5.0
  Súčiastka1 = Arduino Uno (Rev3) - ICSP  # not connected
  L298N1 = L298N DC motor driver
  M1 = DC Motor  # not connected
  M2 = DC Motor  # not connected
  VCC1 = Battery  # not connected
  Súčiastka2 = Bluetooth HC-05 Macho
  J1 = Basic Servo
  hc-sr1 = hc-sr04
  U3 = ESP8266 ESP-01 Upgraded WiFi Module [part_number=ESP8266]  # not connected
  Súčiastka3 = KY-033 Tracing Black White Line Hunting Sensor Module For Arduino
  Súčiastka6 = KY-033 Tracing Black White Line Hunting Sensor Module For Arduino
  Súčiastka7 = KY-033 Tracing Black White Line Hunting Sensor Module For Arduino
  M4 = DC Motor  # not connected
  M3 = DC Motor  # not connected
  U2 = LCD-16X2 [package=lcd-8x2-kit]
  R1 = Rotary Potentiometer (Small) [maximum_resistance=100kΩ package=THT]

nets:
  N1: Mod1.URF01-A0, Mod1.A0-SIG, U2.VO
  N2: Mod1.URF01-A1, Mod1.A1-SIG, U2.R_W
  N3: Mod1.A0-VCC, Mod1.AREF-V, Mod1.SerialLCD-VCC, U2.VSS, U2.A
  N4: Mod1.A0-GND, Mod1.A1-GND, Mod1.AREF-G, Mod1.ParallelLCD-GND, U2.VDD, U2.E, U2.K
  N5: Mod1.A2-SIG, U2.DB5
  N6: Mod1.A3-SIG, U2.DB4
  N7: Mod1.A4-SIG, U2.DB7
  N8: Mod1.A5-SIG, U2.DB6
  N9: Mod1.COM-TX, Mod1.1-S, Súčiastka2.RXD, hc-sr1.Echo
  N10: Mod1.COM-RX, Mod1.0-S, Súčiastka2.TXD, hc-sr1.Trig
  N11: Mod1.9-S, J1.pulse
  N12: Mod1.8-S, Mod1.ParallelLCD-D8, Súčiastka7.S
  N13: Mod1.7-S, Mod1.ParallelLCD-D7, Súčiastka6.S
  N14: Mod1.6-S, Mod1.ParallelLCD-D6, L298N1.ENB
  N15: Mod1.5-S, Súčiastka3.S
  N16: Mod1.3-S, Mod1.SerialLCD-D3, L298N1.ENA
  N17: U2.RS, R1.wiper

notes:
  Na d. pinoch 4 a 2 chýba pripojený ESP8266 3V3 modul ku ktorému je pripojené ESP0-1
  1
  2

custom parts:
  Arduino Sensor Shield v5.0: Arduino Sensor Shield v5.0 provides I2C interface, Bluetooth module communication interface, SD card module communication interface, APC220 wireless RF modules communication interface, RB URF V1.1 ultrasonic sensors interface, 12864 LCD serial and parallel interface, 32 servo controller interfaces. In addition (with the sel jumper removed) allows an external power supply for the servos as the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
  L298N DC motor driver: 2x DC motor driver with 78M05 positive voltage regulator (7..35 V) L298N: max 46 V, 2 A Set 5 V Enable jumper to enable 5 V regultor (needed for the L298N) and +5 V output at screw terminal or supply external +5 V at screw terminal Set ENA and/or ENB to +5 V to enable motor permanently or supply ENA and/or ENB with PWM signal IN1 and IN2 set rotation directory for motor A (OUT1/OUT2) IN2 and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
  ESP8266 ESP-01 Upgraded WiFi Module: Upgraded Version ESP-01,all Flash are upgraded to 1M byte.Also support Cloud service remote transmission.
  KY-033 Tracing Black White Line Hunting Sensor Module For Arduino: Tracing Black White Line Hunting Sensor Module For Arduino Description: This is KY-033 tracking sensor. The KY-033 measures the intensity of infrared radiation and delivers it as an analog output voltage. Features: Operating voltage: 2.5 - 12V(cannot over12V) working current: 18mA-20mA at 5V Enhanced accuracy Documents: http://www.vishay.com/docs/83760/tcrt5000.pdf
