# Fritzing sketch car_connected (saved by Fritzing 0.9.3b)

parts:
  Mod1 = Arduino Sensor Shield v5.0
  Súčiastka1 = Arduino Uno (Rev3) - ICSP  # not connected
  L298N1 = L298N DC motor driver
  M1 = DC Motor  # not connected
  M2 = DC Motor  # not connected
  VCC1 = Battery  # not connected
  Súčiastka2 = Bluetooth HC-05 Macho
  J1 = Basic Servo
  hc-sr1 = hc-sr04
  U3 = ESP8266 ESP-01 Upgraded WiFi Module [part_number=ESP8266]  # not connected
  Súčiastka3 = KY-033 Tracing Black White Line Hunting Sensor Module For Arduino
  Súčiastka6 = KY-033 Tracing Black White Line Hunting Sensor Module For Arduino
  Súčiastka7 = KY-033 Tracing Black White Line Hunting Sensor Module For Arduino
  M4 = DC Motor  # not connected
  M3 = DC Motor  # not connected
  o1 = Module display OLED I2C 128x64 SSD1306 [package=THT]

nets:
  N1: Mod1.A4-SIG, Mod1.IIC-SDA, o1.SDA
  N2: Mod1.A5-SIG, Mod1.IIC-SCL, o1.SCL
  N3: Mod1.COM-TX, Mod1.1-S, Súčiastka2.RXD, hc-sr1.Echo
  N4: Mod1.COM-RX, Mod1.0-S, Súčiastka2.TXD, hc-sr1.Trig
  N5: Mod1.9-S, J1.pulse
  N6: Mod1.8-S, Mod1.ParallelLCD-D8, Súčiastka7.S
  N7: Mod1.7-S, Mod1.ParallelLCD-D7, Súčiastka6.S
  N8: Mod1.6-S, Mod1.ParallelLCD-D6, L298N1.ENB
  N9: Mod1.5-S, Súčiastka3.S
  N10: Mod1.3-S, Mod1.SerialLCD-D3, L298N1.ENA

notes:
  Na d. pinoch 4 a 2 chýba pripojený ESP8266 3V3 modul ku ktorému je pripojené ESP0-1

custom parts:
  Arduino Sensor Shield v5.0: Arduino Sensor Shield v5.0 provides I2C interface, Bluetooth module communication interface, SD card module communication interface, APC220 wireless RF modules communication interface, RB URF V1.1 ultrasonic sensors interface, 12864 LCD serial and parallel interface, 32 servo controller interfaces. In addition (with the sel jumper removed) allows an external power supply for the servos as the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
  L298N DC motor driver: 2x DC motor driver with 78M05 positive voltage regulator (7..35 V) L298N: max 46 V, 2 A Set 5 V Enable jumper to enable 5 V regultor (needed for the L298N) and +5 V output at screw terminal or supply external +5 V at screw terminal Set ENA and/or ENB to +5 V to enable motor permanently or supply ENA and/or ENB with PWM signal IN1 and IN2 set rotation directory for motor A (OUT1/OUT2) IN2 and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
  ESP8266 ESP-01 Upgraded WiFi Module: Upgraded Version ESP-01,all Flash are upgraded to 1M byte.Also support Cloud service remote transmission.
  KY-033 Tracing Black White Line Hunting Sensor Module For Arduino: Tracing Black White Line Hunting Sensor Module For Arduino Description: This is KY-033 tracking sensor. The KY-033 measures the intensity of infrared radiation and delivers it as an analog output voltage. Features: Operating voltage: 2.5 - 12V(cannot over12V) working current: 18mA-20mA at 5V Enhanced accuracy Documents: http://www.vishay.com/docs/83760/tcrt5000.pdf
  Module display OLED I2C 128x64 SSD1306: Ecran OLED I2C SSD163 de 128x64 avec connexion I2C
