# Fritzing sketch zber_dat (saved by Fritzing 0.9.3b)

parts:
  U1 = ESP8266 WiFi Module [part_number=ESP8266]
  S1 = Pushbutton [package="[SMD]"]

nets:
  N1: U1.GPIO_0, S1.Pin_1, S1.Pin_2
  N2: U1.GND, S1.Pin_3

custom parts:
  ESP8266 WiFi Module: Generic WiFi Module based on the ESP8266 with onboard PCB antenna and UART communications
